// Logisim project m1.HPC.MOHAMMEDI.PROJET.ARSHI.circ as structural Verilog: 4 circuits, main circuit main
// UAL
module main (
  input  HORLOGE,
  input  [1:0] CONTROLE_UAL,
  input  CARRY_IN_ADD,
  input  [2:0] Ao,
  input  [2:0] A1,
  input  [2:0] A2,
  input  CARY_IN_SOUS,
  input  Z_IN,
  input  [15:0] DATA,
  input  in_10,
  output [15:0] \Résultat ,
  output zero,
  output overfou,
  output z_out,
  output carry_out
);

  wire [15:0] multiplexer_1_out, registre_file_16_bit_1_out_6, registre_file_16_bit_1_out_7;

  Multiplexer #(.width(16)) multiplexer_1 (
    .in0(DATA), .in1(\Résultat ), .out(multiplexer_1_out), .sel(in_10));  // open: en
  registre_file_16_bit registre_file_16_bit_1 (
    .HORLOGE(HORLOGE), .DONNER(multiplexer_1_out), .A1(A1), .AO(Ao), .A2(A2),
    .out_6(registre_file_16_bit_1_out_6), .out_7(registre_file_16_bit_1_out_7));
  ual_16_bit ual_16_bit_1 (
    .A(registre_file_16_bit_1_out_6), .OPERATION(CONTROLE_UAL), .B(registre_file_16_bit_1_out_7),
    .RESULTA(\Résultat ), .CARRY_IN_ADD(CARRY_IN_ADD), .CARRY_IN_SOUS(CARY_IN_SOUS), .Z_IN(Z_IN),
    .zero(zero), .carry(carry_out), .overflou(overfou), .Z_out(z_out));

  // Notes on the sheet:
  //   00===>ADDITION
  //   01===>soustraction
  //   10===>et
  //   11===>ou
endmodule

module ual_1BIT (
  input  carry_in_add,
  input  A,
  input  B,
  input  ZE,
  input  carry_in_soustra,
  input  [1:0] OPPERATION,
  output CARRY_OUT_add,
  output resulta,
  output carry_out_sustra,
  output Z_OUT
);

  wire adder_1_out, and_1_out, not_1_out, or_1_out, subtractor_1_out;

  Adder #(.width(1)) adder_1 (.a(B), .b(A), .out(adder_1_out), .cin(carry_in_add), .cout(CARRY_OUT_add));
  Subtractor #(.width(1)) subtractor_1 (
    .a(A), .b(B), .out(subtractor_1_out), .bin(carry_in_soustra), .bout(carry_out_sustra));
  and and_1 (and_1_out, A, B);
  or or_1 (or_1_out, A, B);
  Multiplexer #(.select(2), .enable("false")) multiplexer_1 (
    .in0(adder_1_out), .in1(subtractor_1_out), .in2(and_1_out), .in3(or_1_out), .out(resulta),
    .sel(OPPERATION));
  not not_1 (not_1_out, resulta);
  and and_2 (Z_OUT, ZE, not_1_out);
endmodule

// A0
module registre_file_16_bit (
  input  HORLOGE,
  input  [15:0] DONNER,
  input  [2:0] A1,
  input  [2:0] AO,
  input  [2:0] A2,
  output [15:0] out_6,
  output [15:0] out_7
);

  wire and_1_out, and_2_out, and_3_out, and_4_out, and_5_out, and_6_out, and_7_out, and_8_out,
       decoder_1_out0, decoder_1_out1, decoder_1_out2, decoder_1_out3, decoder_1_out4, decoder_1_out5,
       decoder_1_out6, decoder_1_out7;
  wire [15:0] register_1_q, register_2_q, register_3_q, register_4_q, register_5_q, register_6_q,
       register_7_q, register_8_q;

  Decoder #(.select(3)) decoder_1 (
    .out0(decoder_1_out0), .out1(decoder_1_out1), .out2(decoder_1_out2), .out3(decoder_1_out3),
    .out4(decoder_1_out4), .out5(decoder_1_out5), .out6(decoder_1_out6), .out7(decoder_1_out7), .sel(AO));  // open: en
  and and_1 (and_1_out, decoder_1_out0, HORLOGE);
  and and_2 (and_2_out, HORLOGE, decoder_1_out1);
  and and_3 (and_3_out, decoder_1_out2, HORLOGE);
  and and_4 (and_4_out, decoder_1_out3, HORLOGE);
  and and_5 (and_5_out, HORLOGE, decoder_1_out4);
  and and_6 (and_6_out, HORLOGE, decoder_1_out5);
  buf and_7 (and_7_out, decoder_1_out6);  // AND_Gate
  and and_8 (and_8_out, HORLOGE, decoder_1_out7);
  Register #(.width(16)) register_1 (.D(DONNER), .Q(register_1_q), .clk(and_1_out));  // open: en, clr
  Register #(.width(16)) register_2 (.D(DONNER), .Q(register_2_q), .clk(and_2_out));  // open: en, clr
  Register #(.width(16)) register_3 (.D(DONNER), .Q(register_3_q), .clk(and_3_out));  // open: en, clr
  Register #(.width(16)) register_4 (.D(DONNER), .Q(register_4_q), .clk(and_4_out));  // open: en, clr
  Register #(.width(16)) register_5 (.Q(register_5_q), .clk(and_5_out));  // open: D, en, clr
  Register #(.width(16)) register_6 (.D(DONNER), .Q(register_6_q), .clk(and_6_out));  // open: en, clr
  Register #(.width(16)) register_7 (.D(DONNER), .Q(register_7_q), .clk(and_7_out));  // open: en, clr
  Register #(.width(16)) register_8 (.D(DONNER), .Q(register_8_q), .clk(and_8_out));  // open: en, clr
  Multiplexer #(.select(3), .width(16)) multiplexer_1 (
    .in0(register_1_q), .in1(register_2_q), .in2(register_3_q), .in3(register_4_q), .in4(register_5_q),
    .in5(register_6_q), .in6(register_7_q), .in7(register_8_q), .out(out_6), .sel(A1));  // open: en
  Multiplexer #(.select(3), .width(16)) multiplexer_2 (
    .in0(register_1_q), .in1(register_2_q), .in2(register_3_q), .in3(register_4_q), .in4(register_5_q),
    .in5(register_6_q), .in6(register_7_q), .in7(register_8_q), .out(out_7), .sel(A2));  // open: en
endmodule

module ual_16_bit (
  input  Z_IN,
  input  CARRY_IN_SOUS,
  input  CARRY_IN_ADD,
  input  [1:0] OPERATION,
  input  [15:0] A,
  input  [15:0] B,
  output [15:0] RESULTA,
  output zero,
  output overflou,
  output Z_out,
  output carry
);

  wire overflou_soustraction_out, overfou_addition_out, ual_1bit_1_carry_out_add,
       ual_1bit_1_carry_out_sustra, ual_1bit_1_z_out, ual_1bit_2_carry_out_add, ual_1bit_2_carry_out_sustra,
       ual_1bit_2_z_out, ual_1bit_3_carry_out_add, ual_1bit_3_carry_out_sustra, ual_1bit_3_z_out,
       ual_1bit_4_carry_out_add, ual_1bit_4_carry_out_sustra, ual_1bit_4_z_out, ual_1bit_5_carry_out_add,
       ual_1bit_5_carry_out_sustra, ual_1bit_5_z_out, ual_1bit_6_carry_out_add, ual_1bit_6_carry_out_sustra,
       ual_1bit_6_z_out, ual_1bit_7_carry_out_add, ual_1bit_7_carry_out_sustra, ual_1bit_8_carry_out_add,
       ual_1bit_8_carry_out_sustra, ual_1bit_8_z_out, ual_1bit_9_carry_out_add, ual_1bit_9_carry_out_sustra,
       ual_1bit_9_z_out, ual_1bit_10_carry_out_add, ual_1bit_10_carry_out_sustra, ual_1bit_10_z_out,
       ual_1bit_11_carry_out_add, ual_1bit_11_carry_out_sustra, ual_1bit_11_z_out, ual_1bit_12_carry_out_add,
       ual_1bit_12_carry_out_sustra, ual_1bit_12_z_out, ual_1bit_13_carry_out_add,
       ual_1bit_13_carry_out_sustra, ual_1bit_13_z_out, ual_1bit_14_carry_out_add,
       ual_1bit_14_carry_out_sustra, ual_1bit_14_z_out, ual_1bit_15_carry_out_add,
       ual_1bit_15_carry_out_sustra, ual_1bit_15_z_out, ual_1bit_16_carry_out_add,
       ual_1bit_16_carry_out_sustra;

  ual_1BIT ual_1bit_1 (
    .A(A[0]), .B(B[0]), .ZE(Z_IN), .OPPERATION(OPERATION), .carry_in_add(CARRY_IN_ADD),
    .CARRY_OUT_add(ual_1bit_1_carry_out_add), .carry_in_soustra(CARRY_IN_SOUS), .resulta(RESULTA[0]),
    .carry_out_sustra(ual_1bit_1_carry_out_sustra), .Z_OUT(ual_1bit_1_z_out));
  ual_1BIT ual_1bit_2 (
    .A(A[1]), .B(B[1]), .ZE(ual_1bit_1_z_out), .OPPERATION(OPERATION),
    .carry_in_add(ual_1bit_1_carry_out_add), .CARRY_OUT_add(ual_1bit_2_carry_out_add),
    .carry_in_soustra(ual_1bit_1_carry_out_sustra), .resulta(RESULTA[1]),
    .carry_out_sustra(ual_1bit_2_carry_out_sustra), .Z_OUT(ual_1bit_2_z_out));
  ual_1BIT ual_1bit_3 (
    .A(A[2]), .B(B[2]), .ZE(ual_1bit_2_z_out), .OPPERATION(OPERATION),
    .carry_in_add(ual_1bit_2_carry_out_add), .CARRY_OUT_add(ual_1bit_3_carry_out_add),
    .carry_in_soustra(ual_1bit_2_carry_out_sustra), .resulta(RESULTA[2]),
    .carry_out_sustra(ual_1bit_3_carry_out_sustra), .Z_OUT(ual_1bit_3_z_out));
  ual_1BIT ual_1bit_4 (
    .A(A[3]), .B(B[3]), .ZE(ual_1bit_3_z_out), .OPPERATION(OPERATION),
    .carry_in_add(ual_1bit_3_carry_out_add), .CARRY_OUT_add(ual_1bit_4_carry_out_add),
    .carry_in_soustra(ual_1bit_3_carry_out_sustra), .resulta(RESULTA[3]),
    .carry_out_sustra(ual_1bit_4_carry_out_sustra), .Z_OUT(ual_1bit_4_z_out));
  ual_1BIT ual_1bit_5 (
    .A(A[4]), .B(B[4]), .ZE(ual_1bit_4_z_out), .OPPERATION(OPERATION),
    .carry_in_add(ual_1bit_4_carry_out_add), .CARRY_OUT_add(ual_1bit_5_carry_out_add),
    .carry_in_soustra(ual_1bit_4_carry_out_sustra), .resulta(RESULTA[4]),
    .carry_out_sustra(ual_1bit_5_carry_out_sustra), .Z_OUT(ual_1bit_5_z_out));
  ual_1BIT ual_1bit_6 (
    .A(A[5]), .B(B[5]), .ZE(ual_1bit_5_z_out), .OPPERATION(OPERATION),
    .carry_in_add(ual_1bit_5_carry_out_add), .CARRY_OUT_add(ual_1bit_6_carry_out_add),
    .carry_in_soustra(ual_1bit_5_carry_out_sustra), .resulta(RESULTA[5]),
    .carry_out_sustra(ual_1bit_6_carry_out_sustra), .Z_OUT(ual_1bit_6_z_out));
  ual_1BIT ual_1bit_7 (
    .A(A[6]), .B(B[6]), .ZE(ual_1bit_6_z_out), .OPPERATION(OPERATION),
    .carry_in_add(ual_1bit_6_carry_out_add), .CARRY_OUT_add(ual_1bit_7_carry_out_add),
    .carry_in_soustra(ual_1bit_6_carry_out_sustra), .resulta(RESULTA[6]),
    .carry_out_sustra(ual_1bit_7_carry_out_sustra), .Z_OUT(ual_1bit_7_carry_out_sustra));
  ual_1BIT ual_1bit_8 (
    .A(A[7]), .B(B[7]), .ZE(ual_1bit_7_carry_out_sustra), .OPPERATION(OPERATION),
    .carry_in_add(ual_1bit_7_carry_out_add), .CARRY_OUT_add(ual_1bit_8_carry_out_add),
    .carry_in_soustra(ual_1bit_7_carry_out_sustra), .resulta(RESULTA[7]),
    .carry_out_sustra(ual_1bit_8_carry_out_sustra), .Z_OUT(ual_1bit_8_z_out));
  ual_1BIT ual_1bit_9 (
    .A(A[8]), .B(B[8]), .ZE(ual_1bit_8_carry_out_add), .OPPERATION(OPERATION),
    .carry_in_add(ual_1bit_8_z_out), .CARRY_OUT_add(ual_1bit_9_carry_out_add),
    .carry_in_soustra(ual_1bit_8_carry_out_sustra), .resulta(RESULTA[8]),
    .carry_out_sustra(ual_1bit_9_carry_out_sustra), .Z_OUT(ual_1bit_9_z_out));
  ual_1BIT ual_1bit_10 (
    .A(A[9]), .B(B[9]), .ZE(ual_1bit_9_z_out), .OPPERATION(OPERATION),
    .carry_in_add(ual_1bit_9_carry_out_add), .CARRY_OUT_add(ual_1bit_10_carry_out_add),
    .carry_in_soustra(ual_1bit_9_carry_out_sustra), .resulta(RESULTA[9]),
    .carry_out_sustra(ual_1bit_10_carry_out_sustra), .Z_OUT(ual_1bit_10_z_out));
  ual_1BIT ual_1bit_11 (
    .A(A[10]), .B(B[10]), .ZE(ual_1bit_10_z_out), .OPPERATION(OPERATION),
    .carry_in_add(ual_1bit_10_carry_out_add), .CARRY_OUT_add(ual_1bit_11_carry_out_add),
    .carry_in_soustra(ual_1bit_10_carry_out_sustra), .resulta(RESULTA[10]),
    .carry_out_sustra(ual_1bit_11_carry_out_sustra), .Z_OUT(ual_1bit_11_z_out));
  ual_1BIT ual_1bit_12 (
    .A(A[11]), .B(B[11]), .ZE(ual_1bit_11_z_out), .OPPERATION(OPERATION),
    .carry_in_add(ual_1bit_11_carry_out_add), .CARRY_OUT_add(ual_1bit_12_carry_out_add),
    .carry_in_soustra(ual_1bit_11_carry_out_sustra), .resulta(RESULTA[11]),
    .carry_out_sustra(ual_1bit_12_carry_out_sustra), .Z_OUT(ual_1bit_12_z_out));
  ual_1BIT ual_1bit_13 (
    .A(A[12]), .B(B[12]), .ZE(ual_1bit_12_z_out), .OPPERATION(OPERATION),
    .carry_in_add(ual_1bit_12_carry_out_add), .CARRY_OUT_add(ual_1bit_13_carry_out_add),
    .carry_in_soustra(ual_1bit_12_carry_out_sustra), .resulta(RESULTA[12]),
    .carry_out_sustra(ual_1bit_13_carry_out_sustra), .Z_OUT(ual_1bit_13_z_out));
  ual_1BIT ual_1bit_14 (
    .A(A[13]), .B(B[13]), .ZE(ual_1bit_13_z_out), .OPPERATION(OPERATION),
    .carry_in_add(ual_1bit_13_carry_out_add), .CARRY_OUT_add(ual_1bit_14_carry_out_add),
    .carry_in_soustra(ual_1bit_13_carry_out_sustra), .resulta(RESULTA[13]),
    .carry_out_sustra(ual_1bit_14_carry_out_sustra), .Z_OUT(ual_1bit_14_z_out));
  ual_1BIT ual_1bit_15 (
    .A(A[14]), .B(B[14]), .ZE(ual_1bit_14_z_out), .OPPERATION(OPERATION),
    .carry_in_add(ual_1bit_14_carry_out_add), .CARRY_OUT_add(ual_1bit_15_carry_out_add),
    .carry_in_soustra(ual_1bit_14_carry_out_sustra), .resulta(RESULTA[14]),
    .carry_out_sustra(ual_1bit_15_carry_out_sustra), .Z_OUT(ual_1bit_15_z_out));
  ual_1BIT ual_1bit_16 (
    .A(A[15]), .B(B[15]), .ZE(ual_1bit_15_z_out), .OPPERATION(OPERATION),
    .carry_in_add(ual_1bit_15_carry_out_add), .CARRY_OUT_add(ual_1bit_16_carry_out_add),
    .carry_in_soustra(ual_1bit_15_carry_out_sustra), .resulta(RESULTA[15]),
    .carry_out_sustra(ual_1bit_16_carry_out_sustra), .Z_OUT(Z_out));
  or or_1 (carry, ual_1bit_16_carry_out_sustra, ual_1bit_16_carry_out_add);
  xor overflou_soustraction (overflou_soustraction_out, ual_1bit_15_carry_out_sustra, ual_1bit_16_carry_out_sustra);
  xor overfou_addition (overfou_addition_out, ual_1bit_15_z_out, Z_out);
  or or_2 (overflou, overflou_soustraction_out, overfou_addition_out);
  nor nor_1 (zero, RESULTA[0], RESULTA[1], RESULTA[2], RESULTA[3], RESULTA[4], RESULTA[5], RESULTA[6], RESULTA[7], RESULTA[8], RESULTA[9], RESULTA[10], RESULTA[11], RESULTA[12], RESULTA[13], RESULTA[14], RESULTA[15]);

  // Notes on the sheet:
  //   CARRY OUT SOUS
  //   CARRY_OUT_add
endmodule
